# Fritzing sketch circuit diagram (saved by Fritzing 0.9.3b)
breadboards: 1

parts:
  Part1 = Arduino Mega 2560 (Rev3)
  Grove1 = Grove OLED 128x96
  GSM_SIM_GPSR_SMS_SIM900_SIM1 = SIM800L [package=THT]
  NEO6M = SUP500F [package=sup500f]
  e-radionica_com1 = LM393 vibration sensor breakout [part_number=100031]

nets:
  N1: Part1.D21/SCL, Grove1.SCL
  N2: Part1.D20/SDA, Grove1.SDA
  N3: Part1.D19/RX1, GSM_SIM_GPSR_SMS_SIM900_SIM1.SIM_TXD
  N4: Part1.D18/TX1, GSM_SIM_GPSR_SMS_SIM900_SIM1.SIM_RXD
  N5: Part1.D17_PWM/RX2, NEO6M.TX-O
  N6: Part1.D16_PWM/TX2, NEO6M.RX-I
  VCC: Part1.5V, Grove1.VCC, GSM_SIM_GPSR_SMS_SIM900_SIM1.5V, NEO6M.VCC, e-radionica_com1.VCC
  GND: Part1.GND, Grove1.GND, GSM_SIM_GPSR_SMS_SIM900_SIM1.GND, NEO6M.GND, e-radionica_com1.GND
  N7: Part1.D7_PWM, e-radionica_com1.DO
